# Fritzing sketch schematic (saved by Fritzing 0.7.11b)
breadboards: 1

parts:
  1_5_kΩ = Resistor [tolerance=±5% resistance=1.5k package=THT]
  690_Ω = Resistor [tolerance=±5% resistance=680 package=THT]
  1_5_kΩ_2 = Resistor [tolerance=±5% resistance=1.5k package=THT]
  690_Ω_2 = Resistor [tolerance=±5% resistance=680 package=THT]
  1_5_kΩ_3 = Resistor [tolerance=±5% resistance=1.5k package=THT]
  690_Ω_3 = Resistor [tolerance=±5% resistance=680 package=THT]
  HD15 = HD-15
  Arduino = Arduino

nets:
  N1: 1_5_kΩ.Pin_0, 690_Ω.Pin_1, HD15.pin3
  N2: 1_5_kΩ.Pin_1, Arduino.D0RX
  N3: 690_Ω.Pin_0, Arduino.D1TX
  N4: 1_5_kΩ_2.Pin_0, 690_Ω_2.Pin_1, HD15.pin2
  N5: 1_5_kΩ_2.Pin_1, Arduino.D4
  N6: 690_Ω_2.Pin_0, Arduino.D5
  N7: 1_5_kΩ_3.Pin_0, 690_Ω_3.Pin_1, HD15.pin1
  N8: 1_5_kΩ_3.Pin_1, Arduino.D6
  N9: 690_Ω_3.Pin_0, Arduino.D7
  N10: HD15.pin5, Arduino.GND
  N11: HD15.pin13, Arduino.D3
  N12: HD15.pin14, Arduino.D10
